# Fritzing sketch Alhambra-led (saved by Fritzing 0.9.3b)

parts:
  Part1 = iceZUM Alhambra
  LED1 = smd LED [color="Green (560nm)" package="0603 [SMD]"]

nets:
  N1: Part1.G, LED1.anode
  N2: Part1.AR, LED1.cathode

custom parts:
  iceZUM Alhambra: Arduino/zum compatible Open FPGA electronic board. Synthesize hardware easily, using only open source tools
